# Fritzing sketch electric (saved by Fritzing 1.0.1rc)
breadboards: 1

parts:
  元件1 = Arduino Mega 2560 (Rev3)
  元件2 = Bluetooth HC-05 Macho
  BAT1 = Battery Holders [package=lipo-1100mAh]
  BAT2 = Battery Holders [package=lipo-1100mAh]
  e-radionica_com1 = LM393 LDR breakout [part_number=100027]
  M4 = PH meter with sensor in breadboard [package=THT]
  A1 = tds-sensor-meter-v1.0_1
  M1 = DC Motor [voltage_(max)=6V voltage_(min)=3V]
  S1 = H-Bridge with L298N
  M2 = DC Motor [voltage_(max)=6V voltage_(min)=3V]
  S2 = H-Bridge with L298N
  M5 = DC Motor [voltage_(max)=6V voltage_(min)=3V]
  M6 = DC Motor [voltage_(max)=6V voltage_(min)=3V]

nets:
  N1: 元件1.A0, A1.pin1
  N2: 元件1.A1, e-radionica_com1.AO
  N3: 元件1.A2, M4.pin1
  N4: 元件1.D17_PWM/RX2, 元件2.TXD
  N5: 元件1.D16_PWM/TX2, 元件2.RXD
  N6: 元件1.D26, S2.ENA
  N7: 元件1.D28, S2.IN1
  N8: 元件1.D30, S2.IN2
  N9: 元件1.D32, S2.IN3
  N10: 元件1.D34, S2.IN4
  N11: 元件1.D36, S2.ENB
  N12: 元件1.D39, S1.ENA
  N13: 元件1.D41, S1.IN1
  N14: 元件1.D43, S1.IN2
  N15: 元件1.D45, S1.IN3
  N16: 元件1.D47, S1.IN4
  N17: 元件1.D49, S1.ENB
  VCC: 元件2.VCC, e-radionica_com1.VCC, M4.pin2, A1.pin2, S1.5V
  GND: 元件2.GND, BAT2.-, e-radionica_com1.GND, M4.pin3, A1.pin3, S1.GND, S2.GND
  12V: BAT1.+, S1.12V, S2.12V
  N18: M1.pin_1, S1.M1-02
  N19: M1.pin_2, S1.M1-01
  N20: S1.M2-01, M2.pin_2
  N21: S1.M2-02, M2.pin_1
  N22: S2.M1-01, M5.pin_2
  N23: S2.M1-02, S2.M2-01, M5.pin_1, M6.pin_2
  N24: S2.M2-02, M6.pin_1

custom parts:
  PH meter with sensor in breadboard: DFrobot PH meter (SKU SEN0161)
  : TDS Meter V1.0 Development Board Water Meter Filter Measuring Water Sensor Module.
  H-Bridge with L298N: h-bridge
